# Fritzing sketch bipfromrefrigerator (saved by Fritzing 0.9.6b)
circuit board: 3.66845cm x 5.11823cm

parts:
  AFF7SEGS = Grove 4 Digit Display
  VCC1 = Battery block 9V
  ARDUINOUNO = Arduino Uno (Rev3)
  J1 = Piezo Speaker
  T1 = TMP36 Temperature Sensor [package="TO92 [THT]"]

nets:
  GND: AFF7SEGS.GND, VCC1.-, ARDUINOUNO.GND, J1.pin1, T1.GND
  VCC: AFF7SEGS.VCC, VCC1.+, ARDUINOUNO.5V, T1.+Vs
  N1: AFF7SEGS.DIO, ARDUINOUNO.A4/SDA
  N2: AFF7SEGS.CLK, ARDUINOUNO.A5/SCL
  N3: ARDUINOUNO.A3, T1.Vout
  N4: ARDUINOUNO.D2, J1.pin2

// code stored in the sketch: Untitled2.ino
#include <Adafruit_LEDBackpack.h>                                // Inclut la biblioth?que "Adafruit_LEDBackpack" poour utiliser l'afficheur 7 segments ? 4 digits I2C
Adafruit_7segment led_display1 = Adafruit_7segment();            // D?finit le type de l'afficheur 7 segments ? 4 digits I2C
const int STMP = A3;                                             // Cr?e une constante "STMP" de valeur "A3"
const int VCCBUZZER = 2;                                         // Cr?e une constante "VCCBUZZER" de valeur "2"
int c = 0;                                                       // Cr?e une variable "c" de valeur 0
int tmax = 6;                                                    // Cr?e une variable "tmin" de valeur 6
int tmin = 0;                                                    // Cr?e une variable "tmin" de valeur 0
void setup() {                                                   // Dans la fonction "setup()"...
  led_display1.begin(112);                                       // La vitesse du signal de l'afficheur 7 segments ? 4 digits I2C est de 112
  pinMode(STMP, INPUT);                                          // D?finit la broche A3 de l'Arduino UNO en entr?e
  pinMode(VCCBUZZER, OUTPUT);                                    // D?finit la broche 2 de la'Arduino UNO en sortie
  digitalWrite(VCCBUZZER, LOW);                                  // Met la broche 2 ? l'?tat bas (arr?t?)
}                                                                // Fin de la fonction "setup()"
void loop() {                                                    // Dans la fonction "loop()"...
  maj();                                                         // Ex?cuter la fonction "maj()" (pr?cis?e plus tard)
  while (c > tmax) {                                             // Tant que la variable "c" est forc?ment sup?rieure ? la variable "tmax"...
    digitalWrite(VCCBUZZER, HIGH);                               // Met la broche 2 ? l'?tat haut (allum?)
    maj();                                                       // Ex?cuter la fonction "maj()"
    delay(500);                                                  // Attendre 0,5 secondes
    digitalWrite(VCCBUZZER, LOW);                                // Met la broche 2 ? l'?tat bas (arr?t?)
    maj();                                                       // Ex?cuter la fonction "maj()"
    delay(500);                                                  // Attendre 0,5 secondes
  }                                                              // Fin de la boucle while
  while (c <= tmin) {                                            // Tant que la variable "c" est inf?rieure ou ?gale ? la variable "tmin"...
    digitalWrite(VCCBUZZER, HIGH);                               // Met la broche 2 ? l'?tat haut (allum?)
    maj();                                                       // Ex?cuter la fonction "maj()"
    delay(250);                                                  // Attendre 0,25 secondes
    digitalWrite(VCCBUZZER, LOW);                                // Met la broche 2 ? l'?tat bas (arr?t?)
    maj();                                                       // Ex?cuter la fonction "maj()"
    delay(750);                                                  // Attendre 0,25 secondes
  }                                                              // Fin de la boucle while
  delay(500);                                                    // Attendre 0,5 secondes
}                                                                // Fin de la fonction "loop()"
void maj() {                                                     // Dans la fonction "maj()"...
  c = map(((analogRead(STMP) - 20) * 3.04), 0, 1023, -40, 125);  // Mettre ? jour la variable "c"
  led_display1.writeDisplay();                                   // Effacer l'Afficheur l'afficheur 7 segments ? 4 digits I2C
  led_display1.print(c);                                         // Afficher la variable "c" sur l'afficheur 7 segments ? 4 digits I2C
}                                                                // Fin de la fonction "maj()"
